// Logisim project cpu.circ as structural Verilog: 1 circuit, main circuit main
module main (
  input  [31:0] INSTRUCTION,
  input  CLOCK,
  output [31:0] PROGRAM_COUNTER,
  output [31:0] ra,
  output [31:0] sp,
  output [31:0] t0,
  output [31:0] t1,
  output [31:0] t2,
  output [31:0] s0,
  output [31:0] s1,
  output [31:0] a0
);

  wire [11:0] imm;
  wire [19:0] INSTRUCTION2;
  wire [31:0] adder_1_out, Arithmetic_Logic_Unit_result, DMEM_p4, imm_gen_1_imm, multiplexer_1_out,
       multiplexer_2_out, RegFile_read_data_1, RegFile_read_data_2;

  // control_logic control_logic_1: pin names not known
  Adder #(.width(32)) adder_1 (.a(PROGRAM_COUNTER), .b(32'h4), .out(adder_1_out));  // open: cin, cout
  Register #(.width(32), .trigger("falling")) PC (
    .D(adder_1_out), .en(1'b1), .clk(CLOCK), .Q(PROGRAM_COUNTER));  // open: clr
  fallingsadness fallingsadness_1 (
    .clk(CLOCK), .WE(1'b1), .in_4(INSTRUCTION), .out_5({imm, INSTRUCTION2}));  // open: reset
  imm_gen imm_gen_1 (.imm(imm_gen_1_imm), .inst({imm, INSTRUCTION2}));  // open: ImmSel
  // branch_comp branch_comp_1: pin names not known
  regfile_main RegFile (
    .rd(INSTRUCTION2[11:7]), .Read_Data_1(RegFile_read_data_1), .Read_Data_2(RegFile_read_data_2), .ra(ra),
    .sp(sp), .t0(t0), .t1(t1), .t2(t2), .s0(s0), .s1(s1), .a0(a0), .rs1(INSTRUCTION2[19:15]),
    .Write_Data(multiplexer_2_out), .RegWEn(1'b1), .clk(CLOCK));  // open: rs2
  Multiplexer #(.width(32), .enable("false")) multiplexer_1 (
    .in0(RegFile_read_data_2), .in1(imm_gen_1_imm), .out(multiplexer_1_out), .sel(1'b1));
  alu Arithmetic_Logic_Unit (
    .ALUSel(4'b0000), .Result(Arithmetic_Logic_Unit_result), .A(RegFile_read_data_1), .B(multiplexer_1_out));
  // mem_main DMEM: pin names not known; wires that end beside it: Arithmetic_Logic_Unit_result, RegFile_read_data_2, CLOCK, DMEM_p4
  Multiplexer #(.width(32), .enable("false")) multiplexer_2 (
    .in0(DMEM_p4), .in1(Arithmetic_Logic_Unit_result), .out(multiplexer_2_out), .sel(1'b1));

  // Other names for the same wires on the sheet: clk = CLOCK; opcode[6:0] = INSTRUCTION2[6:0];
  //   rd[4:0] = INSTRUCTION2[11:7]; textttfunct3[2:0] = INSTRUCTION2[14:12]; rs1[4:0] = INSTRUCTION2[19:15];
  //   INSTRUCTION2[31:20] = imm

  // Notes on the sheet:
  //   Output
  //   IMEM (do **NOT** move this)
  //   Inputs
  //   It is OK to move the PC, RegFile, ALU, MEM, Branch Comp, Imm Gen, and Control Logic to wherever is most convenient for you when constructing your CPU, and to delete this text
  //   Inputs/Outputs for testing. Do **NOT** move these.
endmodule
